// Logisim project Loesungen.circ as structural Verilog: 8 circuits, main circuit ClockDivider_Custom
module ClockDivider_Custom (
);

  wire clock_1_out, clock_2_out;
  wire [3:0] cntr_1_cnt_out;

  Clock clock_1 (.out(clock_1_out));
  Clock clock_2 (.out(clock_2_out));
  Cntr cntr_1 (.Clk(clock_1_out), .Cnt_Out(cntr_1_cnt_out));
  // Digital_Oscilloscope digital_oscilloscope_1: pin names not known; wires that end beside it: clock_2_out, cntr_1_cnt_out[0], cntr_1_cnt_out[1], cntr_1_cnt_out[2], cntr_1_cnt_out[3]
endmodule

module ClockDivider_LogisimCnt (
);

  wire clock_1_out, clock_2_out;
  wire [3:0] counter_1_q;

  Counter #(.max('hf), .width(4)) counter_1 (
    .clr(1'b0), .load(1'b0), .up(1'b1), .count(1'b1), .clk(clock_1_out), .Q(counter_1_q));  // open: D, carry
  Clock clock_1 (.out(clock_1_out));
  Clock clock_2 (.out(clock_2_out));
  // Digital_Oscilloscope digital_oscilloscope_1: pin names not known; wires that end beside it: clock_2_out, counter_1_q[0], counter_1_q[1], counter_1_q[2], counter_1_q[3]
endmodule

module ClockDivider_Thirds (
);

  wire and_1_out, and_2_out, clock_1_out, clock_2_out, counter_1_carry, not_1_out, not_2_out, not_3_out,
       not_4_out, not_5_out, not_6_out, or_1_out, t_ff_1_q;
  wire [1:0] counter_1_q;

  Clock clock_1 (.out(clock_1_out));
  not not_1 (not_1_out, clock_1_out);
  not not_2 (not_2_out, clock_1_out);
  not not_3 (not_3_out, not_1_out);
  not not_4 (not_4_out, not_3_out);
  not not_5 (not_5_out, not_2_out);
  not not_6 (not_6_out, not_5_out);
  and and_1 (and_1_out, not_4_out, clock_1_out);
  and and_2 (and_2_out, ~not_6_out, ~clock_1_out);  // AND_Gate
  or or_1 (or_1_out, and_1_out, and_2_out);
  Counter #(.max('h3), .width(2)) counter_1 (
    .load(counter_1_carry), .up(1'b1), .count(1'b1), .clk(or_1_out), .D(2'b01), .carry(counter_1_carry),
    .Q(counter_1_q));  // open: clr
  T_Flip_Flop t_ff_1 (.T(counter_1_carry), .clk(counter_1_carry), .Q(t_ff_1_q));  // open: Qn, reset, preset
  Clock clock_2 (.out(clock_2_out));
  // Digital_Oscilloscope digital_oscilloscope_1: pin names not known; wires that end beside it: counter_1_q, clock_2_out, counter_1_carry, t_ff_1_q

  // Notes on the sheet:
  //   Diese Aufgabe war ein bisschen komplzierter als ich es wollte, 
  //   da ich dachte die Logisim Counter können "dual edge" zählen (auf beide Flanken)
  //   Da dies nicht möglich ist erzeugt die Schaltung links bei positiver und negativer 
  //   Flanke einen kurzen Puls, der dann vom Counter jeweils als positive Flanke gesehen wird.
endmodule

module Cntr (
  input  Clk,
  output [3:0] Cnt_Out
);

  wire and_1_out, and_2_out, d_ff_1_qn, xor_1_out, xor_2_out, xor_3_out;

  D_Flip_Flop d_ff_1 (.D(d_ff_1_qn), .clk(Clk), .Q(Cnt_Out[0]), .Qn(d_ff_1_qn));  // open: preset, reset
  xor xor_1 (xor_1_out, Cnt_Out[1], Cnt_Out[0]);
  D_Flip_Flop d_ff_2 (.D(xor_1_out), .clk(Clk), .Q(Cnt_Out[1]));  // open: Qn, preset, reset
  and and_1 (and_1_out, Cnt_Out[0], Cnt_Out[1]);
  D_Flip_Flop d_ff_3 (.D(xor_2_out), .clk(Clk), .Q(Cnt_Out[2]));  // open: Qn, preset, reset
  xor xor_2 (xor_2_out, Cnt_Out[2], and_1_out);
  and and_2 (and_2_out, Cnt_Out[0], Cnt_Out[1], Cnt_Out[2]);
  xor xor_3 (xor_3_out, Cnt_Out[3], and_2_out);
  D_Flip_Flop d_ff_4 (.D(xor_3_out), .clk(Clk), .Q(Cnt_Out[3]));  // open: Qn, preset, reset
endmodule

module Milchschaeumer (
);

  wire ausgangsschaltung_1_led1, ausgangsschaltung_1_led2, ausgangsschaltung_1_led3,
       ausgangsschaltung_1_led4, eingangsschaltung_1_l0, eingangsschaltung_1_l1, eingangsschaltung_1_w0,
       Reset_out, T1_out, T2_out, T3_out, T4_out, unit_1_enabled, unit_1_ol0, unit_1_ol1, unit_1_ow0;

  Button T1 (.out(T1_out));
  Button T2 (.out(T2_out));
  Button T3 (.out(T3_out));
  Button T4 (.out(T4_out));
  Button Reset (.out(Reset_out));
  Eingangsschaltung eingangsschaltung_1 (
    .T1(T1_out), .T2(T2_out), .T3(T3_out), .T4(T4_out), .L0(eingangsschaltung_1_l0),
    .L1(eingangsschaltung_1_l1), .W0(eingangsschaltung_1_w0));
  Unit unit_1 (
    .L0(eingangsschaltung_1_l0), .L1(eingangsschaltung_1_l1), .W0(eingangsschaltung_1_w0), .Reset(Reset_out),
    .ENABLED(unit_1_enabled), .OL0(unit_1_ol0), .OL1(unit_1_ol1), .OW0(unit_1_ow0));
  Ausgangsschaltung ausgangsschaltung_1 (
    .ENABLED(unit_1_enabled), .OL0(unit_1_ol0), .OL1(unit_1_ol1), .OW0(unit_1_ow0),
    .LED1(ausgangsschaltung_1_led1), .LED2(ausgangsschaltung_1_led2), .LED3(ausgangsschaltung_1_led3),
    .LED4(ausgangsschaltung_1_led4));
  LED LED1 (.in(ausgangsschaltung_1_led1));
  LED LED2 (.in(ausgangsschaltung_1_led2));
  LED LED3 (.in(ausgangsschaltung_1_led3));
  LED LED4 (.in(ausgangsschaltung_1_led4));

  // Notes on the sheet:
  //   Drücke Reset, um zu simulieren, dass die "Unit" fertig geschäumt hat
endmodule

module Unit (
  input  L0,
  input  L1,
  input  W0,
  input  Reset,
  output ENABLED,
  output OL0,
  output OL1,
  output OW0
);

  wire and_1_out, or_1_out;

  or or_1 (or_1_out, L0, L1, W0);
  and and_1 (and_1_out, ~ENABLED, or_1_out);  // AND_Gate
  S_R_Flip_Flop s_r_ff_1 (.S(L0), .R(1'b0), .clk(and_1_out), .Q(OL0), .reset(Reset));  // open: Qn, preset
  S_R_Flip_Flop s_r_ff_2 (.S(L1), .R(1'b0), .clk(and_1_out), .Q(OL1), .reset(Reset));  // open: Qn, preset
  S_R_Flip_Flop s_r_ff_3 (.S(W0), .R(1'b0), .clk(and_1_out), .Q(OW0), .reset(Reset));  // open: Qn, preset
  or or_2 (ENABLED, OL0, OL1, OW0);
endmodule

module Eingangsschaltung (
  input  T1,
  input  T2,
  input  T3,
  input  T4,
  output L0,
  output L1,
  output W0
);

  or or_1 (L0, T2, T4);
  or or_2 (L1, T3, T4);
  or or_3 (W0, T1, T2, T3);

  // Notes on the sheet:
  //   Ansteuerungsschaltung
endmodule

module Ausgangsschaltung (
  input  ENABLED,
  input  OL0,
  input  OL1,
  input  OW0,
  output LED1,
  output LED2,
  output LED3,
  output LED4
);

  and and_1 (LED1, ~OL0, ~OL1, OW0);  // AND_Gate
  and and_2 (LED2, OL0, ~OL1, OW0);  // AND_Gate
  and and_3 (LED3, ~OL0, OL1, OW0);  // AND_Gate
  and and_4 (LED4, OL0, OL1, ~OW0);  // AND_Gate
endmodule
