// Logisim project Unit.circ as structural Verilog: 2 circuits, main circuit Unit
module Unit (
  input  L0,
  input  L1,
  input  W0,
  input  Reset,
  output ENABLED,
  output OL0,
  output OL1,
  output OW0
);

  wire and_1_out, or_1_out, or_2_out, or_3_out, s_r_ff_1_q, s_r_ff_2_q, s_r_ff_3_q, timer_1_loaded,
       timer_1_trigger;

  S_R_Flip_Flop s_r_ff_1 (.Q(s_r_ff_1_q), .reset(or_1_out), .preset(L0));  // open: S, R, clk, Qn
  S_R_Flip_Flop s_r_ff_2 (.Q(s_r_ff_2_q), .reset(or_1_out), .preset(L1));  // open: S, R, clk, Qn
  S_R_Flip_Flop s_r_ff_3 (.Q(s_r_ff_3_q), .reset(or_1_out), .preset(W0));  // open: S, R, clk, Qn
  or or_1 (or_1_out, Reset, timer_1_loaded);
  or or_2 (or_2_out, Reset, timer_1_trigger);
  or or_3 (or_3_out, s_r_ff_1_q, s_r_ff_2_q, s_r_ff_3_q);
  and and_1 (and_1_out, ~ENABLED, or_3_out);  // AND_Gate
  Timer timer_1 (
    .Reset(Reset), .In0(s_r_ff_3_q), .In1(s_r_ff_1_q), .In2(s_r_ff_2_q), .Trigger(timer_1_trigger),
    .Loaded(timer_1_loaded));
  S_R_Flip_Flop s_r_ff_4 (.S(s_r_ff_1_q), .R(1'b0), .clk(and_1_out), .Q(OL0), .reset(or_2_out));  // open: Qn, preset
  S_R_Flip_Flop s_r_ff_5 (.S(s_r_ff_2_q), .R(1'b0), .clk(and_1_out), .Q(OL1), .reset(or_2_out));  // open: Qn, preset
  S_R_Flip_Flop s_r_ff_6 (.S(s_r_ff_3_q), .R(1'b0), .clk(and_1_out), .Q(OW0), .reset(or_2_out));  // open: Qn, preset
  or or_4 (ENABLED, OL0, OL1, OW0);
endmodule

module Timer (
  input  Reset,
  input  In0,
  input  In1,
  input  In2,
  output Trigger,
  output Loaded
);

  wire clock_1_out, counter_1_carry, not_1_out, not_2_out, not_3_out, not_4_out, or_1_out;
  wire [7:0] multiplier_1_out;

  or or_1 (or_1_out, In0, In1, In2);
  Clock clock_1 (.out(clock_1_out));
  Multiplier multiplier_1 (.a({{5{1'b0}}, In2, In1, 1'b1}), .b(8'h1), .out(multiplier_1_out));  // open: cin, cout
  // Probe on multiplier_1_out
  Counter counter_1 (
    .clr(Reset), .load(or_1_out), .up(1'b0), .count(not_1_out), .clk(clock_1_out), .D(multiplier_1_out),
    .carry(counter_1_carry));  // open: Q
  not not_1 (not_1_out, counter_1_carry);
  not not_2 (not_2_out, counter_1_carry);
  not not_3 (not_3_out, not_2_out);
  not not_4 (not_4_out, not_3_out);
  and and_1 (Trigger, not_4_out, counter_1_carry);
  not not_5 (Loaded, counter_1_carry);
endmodule
