// Logisim project Labor3.circ as structural Verilog
module Register_8Bit (
  input  [7:0] In_8Bit,
  input  CLK,
  input  Reset,
  output [7:0] Out_8Bit
);

  D_Flip_Flop d_ff_1 (.D(In_8Bit[0]), .clk(CLK), .Q(Out_8Bit[0]), .reset(Reset));  // open: Qn, preset
  D_Flip_Flop d_ff_2 (.D(In_8Bit[1]), .clk(CLK), .Q(Out_8Bit[1]), .reset(Reset));  // open: Qn, preset
  D_Flip_Flop d_ff_3 (.D(In_8Bit[2]), .clk(CLK), .Q(Out_8Bit[2]), .reset(Reset));  // open: Qn, preset
  D_Flip_Flop d_ff_4 (.D(In_8Bit[3]), .clk(CLK), .Q(Out_8Bit[3]), .reset(Reset));  // open: Qn, preset
  D_Flip_Flop d_ff_5 (.D(In_8Bit[4]), .clk(CLK), .Q(Out_8Bit[4]), .reset(Reset));  // open: Qn, preset
  D_Flip_Flop d_ff_6 (.D(In_8Bit[5]), .clk(CLK), .Q(Out_8Bit[5]), .reset(Reset));  // open: Qn, preset
  D_Flip_Flop d_ff_7 (.D(In_8Bit[6]), .clk(CLK), .Q(Out_8Bit[6]), .reset(Reset));  // open: Qn, preset
  D_Flip_Flop d_ff_8 (.D(In_8Bit[7]), .clk(CLK), .Q(Out_8Bit[7]), .reset(Reset));  // open: Qn, preset
endmodule

module Shift_Reg_8Bit (
  input  [7:0] ParallelIN,
  input  SerialIN,
  input  CLK,
  input  SHIFT_LOAD,
  input  Reset,
  output [7:0] ParallelOUT,
  output SerialOUT
);

  wire and_1_out, and_2_out, and_3_out, and_4_out, and_5_out, and_6_out, and_7_out, and_8_out, and_9_out,
       and_10_out, and_11_out, and_12_out, and_13_out, and_14_out, and_15_out, and_16_out, and_17_out,
       or_1_out, or_2_out, or_3_out, or_4_out, or_5_out, or_6_out, or_7_out, or_8_out;

  and and_1 (and_1_out, CLK, ~SHIFT_LOAD);  // AND_Gate
  and and_2 (and_2_out, SHIFT_LOAD, ParallelIN[0]);
  D_Flip_Flop d_ff_1 (
    .D(SerialIN), .clk(and_1_out), .Q(ParallelOUT[0]), .preset(and_2_out), .reset(or_1_out));  // open: Qn
  or or_1 (or_1_out, and_3_out, Reset);
  and and_3 (and_3_out, ~ParallelIN[0], SHIFT_LOAD);  // AND_Gate
  and and_4 (and_4_out, SHIFT_LOAD, ParallelIN[1]);
  D_Flip_Flop d_ff_2 (
    .D(ParallelOUT[0]), .clk(and_1_out), .Q(ParallelOUT[1]), .preset(and_4_out), .reset(or_2_out));  // open: Qn
  or or_2 (or_2_out, and_5_out, Reset);
  and and_5 (and_5_out, ~ParallelIN[1], SHIFT_LOAD);  // AND_Gate
  and and_6 (and_6_out, SHIFT_LOAD, ParallelIN[2]);
  D_Flip_Flop d_ff_3 (
    .D(ParallelOUT[1]), .clk(and_1_out), .Q(ParallelOUT[2]), .preset(and_6_out), .reset(or_3_out));  // open: Qn
  or or_3 (or_3_out, and_7_out, Reset);
  and and_7 (and_7_out, ~ParallelIN[2], SHIFT_LOAD);  // AND_Gate
  D_Flip_Flop d_ff_4 (
    .D(ParallelOUT[2]), .clk(and_1_out), .Q(ParallelOUT[3]), .preset(and_9_out), .reset(or_4_out));  // open: Qn
  and and_8 (and_8_out, ~ParallelIN[3], SHIFT_LOAD);  // AND_Gate
  and and_9 (and_9_out, SHIFT_LOAD, ParallelIN[3]);
  or or_4 (or_4_out, and_8_out, Reset);
  and and_10 (and_10_out, SHIFT_LOAD, ParallelIN[4]);
  D_Flip_Flop d_ff_5 (
    .D(ParallelOUT[3]), .clk(and_1_out), .Q(ParallelOUT[4]), .preset(and_10_out), .reset(or_5_out));  // open: Qn
  or or_5 (or_5_out, and_11_out, Reset);
  and and_11 (and_11_out, ~ParallelIN[4], SHIFT_LOAD);  // AND_Gate
  and and_12 (and_12_out, SHIFT_LOAD, ParallelIN[5]);
  D_Flip_Flop d_ff_6 (
    .D(ParallelOUT[4]), .clk(and_1_out), .Q(ParallelOUT[5]), .preset(and_12_out), .reset(or_6_out));  // open: Qn
  or or_6 (or_6_out, and_13_out, Reset);
  and and_13 (and_13_out, ~ParallelIN[5], SHIFT_LOAD);  // AND_Gate
  and and_14 (and_14_out, SHIFT_LOAD, ParallelIN[6]);
  D_Flip_Flop d_ff_7 (
    .D(ParallelOUT[5]), .clk(and_1_out), .Q(ParallelOUT[6]), .preset(and_14_out), .reset(or_7_out));  // open: Qn
  or or_7 (or_7_out, and_15_out, Reset);
  and and_15 (and_15_out, ~ParallelIN[6], SHIFT_LOAD);  // AND_Gate
  and and_16 (and_16_out, SHIFT_LOAD, ParallelIN[7]);
  D_Flip_Flop d_ff_8 (
    .D(ParallelOUT[6]), .clk(and_1_out), .Q(ParallelOUT[7]), .preset(and_16_out), .reset(or_8_out));  // open: Qn
  or or_8 (or_8_out, and_17_out, Reset);
  and and_17 (and_17_out, ~ParallelIN[7], SHIFT_LOAD);  // AND_Gate

  assign SerialOUT = ParallelOUT[7];
endmodule

module Test_Shift_Reg_8Bit (
);

  wire button_1_out, clock_1_out, dipswitch_2_p1, dipswitch_2_p2, shift_reg_8bit_1_serialout;
  wire [7:0] shift_reg_8bit_1_parallelout, undriven;

  // DipSwitch dipswitch_1: pin names not known
  // DipSwitch #(.number(2)) dipswitch_2: pin names not known; wires that end beside it: dipswitch_2_p1, dipswitch_2_p2
  Clock clock_1 (.out(clock_1_out));
  Button button_1 (.out(button_1_out));
  Shift_Reg_8Bit shift_reg_8bit_1 (
    .ParallelIN(undriven), .SerialIN(dipswitch_2_p1), .CLK(clock_1_out), .SHIFT_LOAD(dipswitch_2_p2),
    .Reset(button_1_out), .ParallelOUT(shift_reg_8bit_1_parallelout), .SerialOUT(shift_reg_8bit_1_serialout));
  // Probe on shift_reg_8bit_1_parallelout
  // Probe on shift_reg_8bit_1_serialout
endmodule

module Slave (
  input  DataIn,
  input  Clk,
  input  Sel,
  input  Reset,
  input  ResDatRdy,
  output [7:0] Data,
  output Data_Ready
);

  wire and_1_out, and_2_out, and_3_out, and_4_out, counter_1_carry, or_1_out, or_2_out, s_r_ff_1_q;
  wire [2:0] counter_1_q;
  wire [7:0] shift_reg_8bit_1_parallelout;

  and and_1 (and_1_out, DataIn, Sel);
  and and_2 (and_2_out, Clk, Sel);
  Counter #(.max('h7), .width(3)) counter_1 (
    .clr(Reset), .clk(and_2_out), .carry(counter_1_carry), .Q(counter_1_q));  // open: load, up, count, D
  Shift_Reg_8Bit shift_reg_8bit_1 (
    .SerialIN(and_1_out), .CLK(and_2_out), .Reset(Reset), .ParallelOUT(shift_reg_8bit_1_parallelout));  // open: ParallelIN, SHIFT_LOAD, SerialOUT
  S_R_Flip_Flop s_r_ff_1 (.Q(s_r_ff_1_q), .reset(or_2_out), .preset(counter_1_carry));  // open: S, R, clk, Qn
  or or_1 (or_1_out, Reset, ResDatRdy);
  and and_3 (and_3_out, ~counter_1_q[0], ~counter_1_q[1], ~counter_1_q[2], and_2_out);  // AND_Gate
  S_R_Flip_Flop s_r_ff_2 (.Q(Data_Ready), .reset(or_1_out), .preset(and_4_out));  // open: S, R, clk, Qn
  and and_4 (and_4_out, s_r_ff_1_q, and_3_out);
  or or_2 (or_2_out, Data_Ready, Reset);
  Register_8Bit register_8bit_1 (
    .In_8Bit(shift_reg_8bit_1_parallelout), .CLK(and_3_out), .Reset(Reset), .Out_8Bit(Data));
endmodule

module Master (
  input  [7:0] Data_In,
  input  Clk,
  input  Set,
  input  Reset,
  input  SlaveSelect,
  output DataOut,
  output SS0,
  output SS1
);

  Shift_Reg_8Bit shift_reg_8bit_1 (
    .ParallelIN(Data_In), .CLK(Clk), .SHIFT_LOAD(Set), .Reset(Reset), .SerialOUT(DataOut));  // open: SerialIN, ParallelOUT
  not not_1 (SS0, SlaveSelect);

  assign SS1 = SlaveSelect;
endmodule

module SPI_Uebung (
  input  [7:0] in_1,
  input  SlaveSelect
);

  wire clock_1_out, master_1_dataout, master_1_ss0, master_1_ss1, Reset_out, ResetDataReady_out, SetData_out,
       slave_1_data_ready, slave_2_data_ready;
  wire [7:0] slave_1_data, slave_2_data;

  // Probe on in_1
  Clock clock_1 (.out(clock_1_out));
  Button SetData (.out(SetData_out));
  Button Reset (.out(Reset_out));
  Button ResetDataReady (.out(ResetDataReady_out));
  Master master_1 (
    .Data_In(in_1), .Clk(clock_1_out), .Set(SetData_out), .Reset(Reset_out), .SlaveSelect(SlaveSelect),
    .DataOut(master_1_dataout), .SS0(master_1_ss0), .SS1(master_1_ss1));
  // Probe on slave_1_data
  Slave slave_1 (
    .DataIn(master_1_dataout), .Clk(clock_1_out), .Sel(master_1_ss0), .Reset(Reset_out),
    .ResDatRdy(ResetDataReady_out), .Data(slave_1_data), .Data_Ready(slave_1_data_ready));
  // Probe on slave_1_data_ready
  // Probe on slave_2_data
  Slave slave_2 (
    .DataIn(master_1_dataout), .Clk(clock_1_out), .Sel(master_1_ss1), .Reset(Reset_out),
    .ResDatRdy(ResetDataReady_out), .Data(slave_2_data), .Data_Ready(slave_2_data_ready));
  // Probe on slave_2_data_ready
endmodule

module SPI (
  input  [7:0] in_1,
  input  SlaveSelect
);

  wire clock_1_out, master_1_dataout, master_1_ss0, master_1_ss1, Reset_out, ResetDataReady_out, SetData_out,
       slave_1_data_ready, slave_2_data_ready;
  wire [7:0] slave_1_data, slave_2_data;

  // Probe on in_1
  Clock clock_1 (.out(clock_1_out));
  Button SetData (.out(SetData_out));
  Button Reset (.out(Reset_out));
  Button ResetDataReady (.out(ResetDataReady_out));
  Master master_1 (
    .Data_In(in_1), .Clk(clock_1_out), .Set(SetData_out), .Reset(Reset_out), .SlaveSelect(SlaveSelect),
    .DataOut(master_1_dataout), .SS0(master_1_ss0), .SS1(master_1_ss1));
  Slave slave_1 (
    .DataIn(master_1_dataout), .Clk(clock_1_out), .Sel(master_1_ss0), .Reset(Reset_out),
    .ResDatRdy(ResetDataReady_out), .Data(slave_1_data), .Data_Ready(slave_1_data_ready));
  // Probe on slave_1_data_ready
  Slave slave_2 (
    .DataIn(master_1_dataout), .Clk(clock_1_out), .Sel(master_1_ss1), .Reset(Reset_out),
    .ResDatRdy(ResetDataReady_out), .Data(slave_2_data), .Data_Ready(slave_2_data_ready));
  // Probe on slave_2_data_ready
  TTY tty_1 (.data(slave_1_data[6:0]), .clk(ResetDataReady_out), .clr(Reset_out));  // open: we
  TTY tty_2 (.data(slave_2_data[6:0]), .clk(ResetDataReady_out), .clr(Reset_out));  // open: we
endmodule

module Slave_BiDirec (
  input  [7:0] LoadData,
  input  SetData,
  input  MOSI,
  input  Clk,
  input  Sel,
  input  Reset,
  input  ResDatRdy,
  output MISO,
  output [7:0] DataOUT,
  output Data_Ready
);

  wire and_1_out, and_2_out, and_3_out, and_4_out, counter_1_carry, or_1_out, or_2_out, s_r_ff_1_q;
  wire [2:0] counter_1_q;
  wire [7:0] shift_reg_8bit_1_parallelout;

  and and_1 (and_1_out, MOSI, Sel);
  and and_2 (and_2_out, Clk, Sel);
  Counter #(.max('h7), .width(3)) counter_1 (
    .clr(Reset), .clk(and_2_out), .carry(counter_1_carry), .Q(counter_1_q));  // open: load, up, count, D
  Shift_Reg_8Bit shift_reg_8bit_1 (
    .ParallelIN(LoadData), .SerialIN(and_1_out), .CLK(and_2_out), .SHIFT_LOAD(SetData), .Reset(Reset),
    .ParallelOUT(shift_reg_8bit_1_parallelout), .SerialOUT(MISO));
  S_R_Flip_Flop s_r_ff_1 (.Q(s_r_ff_1_q), .reset(or_2_out), .preset(counter_1_carry));  // open: S, R, clk, Qn
  or or_1 (or_1_out, Reset, ResDatRdy);
  and and_3 (and_3_out, ~counter_1_q[0], ~counter_1_q[1], ~counter_1_q[2], and_2_out);  // AND_Gate
  S_R_Flip_Flop s_r_ff_2 (.Q(Data_Ready), .reset(or_1_out), .preset(and_4_out));  // open: S, R, clk, Qn
  and and_4 (and_4_out, s_r_ff_1_q, and_3_out);
  or or_2 (or_2_out, Data_Ready, Reset);
  Register_8Bit register_8bit_1 (
    .In_8Bit(shift_reg_8bit_1_parallelout), .CLK(and_3_out), .Reset(Reset), .Out_8Bit(DataOUT));
endmodule

module Master_BiDirec (
  input  [7:0] Data_In,
  input  MISO,
  input  Clk,
  input  Set,
  input  Reset,
  input  SlaveSelect,
  output MOSI,
  output SS0,
  output SS1
);

  Shift_Reg_8Bit shift_reg_8bit_1 (
    .ParallelIN(Data_In), .SerialIN(MISO), .CLK(Clk), .SHIFT_LOAD(Set), .Reset(Reset), .SerialOUT(MOSI));  // open: ParallelOUT
  not not_1 (SS0, SlaveSelect);

  assign SS1 = SlaveSelect;
endmodule
