// Logisim project SpektrumAnalyzerFSM.circ as structural Verilog: 11 circuits, main circuit main
module main (
  input  in_1
);

  wire button_1_out, clock_1_out, dipswitch_1_p1, dipswitch_1_p2, dipswitch_1_p3, dipswitch_1_p4,
       dipswitch_1_p5, dipswitch_1_p6, not_1_out, spektrumanalyzerfsm_1_idle,
       spektrumanalyzerfsm_1_measurment, spektrumanalyzerfsm_1_processing, spektrumanalyzerfsm_1_sethw,
       spektrumanalyzerfsm_1_transfer;

  not not_1 (not_1_out, in_1);
  // DipSwitch #(.number(6)) dipswitch_1: pin names not known; wires that end beside it: dipswitch_1_p1, dipswitch_1_p2, dipswitch_1_p3, dipswitch_1_p4, dipswitch_1_p5, dipswitch_1_p6
  Clock clock_1 (.out(clock_1_out));
  Button button_1 (.out(button_1_out));
  LedBar #(.matrixcols(5)) ledbar_1 (
    .led0(spektrumanalyzerfsm_1_idle), .led1(spektrumanalyzerfsm_1_sethw),
    .led2(spektrumanalyzerfsm_1_measurment), .led3(spektrumanalyzerfsm_1_transfer),
    .led4(spektrumanalyzerfsm_1_processing));
  SpektrumAnalyzerFSM spektrumanalyzerfsm_1 (
    .SingleShot(not_1_out), .Cont(in_1), .Start(dipswitch_1_p1), .Abort(dipswitch_1_p2),
    .HwReady(dipswitch_1_p3), .Captured(dipswitch_1_p4), .TransferDone(dipswitch_1_p5),
    .Displayed(dipswitch_1_p6), .Clk(clock_1_out), .Reset(button_1_out), .Idle(spektrumanalyzerfsm_1_idle),
    .SetHw(spektrumanalyzerfsm_1_sethw), .Measurment(spektrumanalyzerfsm_1_measurment),
    .Transfer(spektrumanalyzerfsm_1_transfer), .Processing(spektrumanalyzerfsm_1_processing));
endmodule

module SpektrumAnalyzerFSM (
  input  SingleShot,
  input  Cont,
  input  Start,
  input  Abort,
  input  HwReady,
  input  Captured,
  input  TransferDone,
  input  Displayed,
  input  Clk,
  input  Reset,
  output Idle,
  output SetHw,
  output Measurment,
  output Transfer,
  output Processing
);

  wire [2:0] inputlogic_1_newstate, register_1_q;

  InputLogic inputlogic_1 (
    .OldState(register_1_q), .SingleShot(SingleShot), .Cont(Cont), .Start(Start), .Abort(Abort),
    .HwReady(HwReady), .Capture(Captured), .Transfer(TransferDone), .Displayed(Displayed),
    .NewState(inputlogic_1_newstate));
  Register #(.width(3)) register_1 (.D(inputlogic_1_newstate), .clk(Clk), .Q(register_1_q), .clr(Reset));  // open: en
  OutputLogic outputlogic_1 (.StateIn(register_1_q), .Decoded({Processing, Transfer, Measurment, SetHw, Idle}));
endmodule

module StartEvent (
  input  [2:0] StateIN,
  output [2:0] StateOUT
);

  wire and_1_out;

  and and_1 (and_1_out, ~StateIN[2], ~StateIN[1]);  // AND_Gate
  or or_1 (StateOUT[0], and_1_out, StateIN[0]);

  assign StateOUT[2:1] = StateIN[2:1];
endmodule

module AbortEvent (
  output [2:0] StateOUT
);


  assign StateOUT = 3'b000;
endmodule

module InputLogic (
  input  [2:0] OldState,
  input  SingleShot,
  input  Cont,
  input  Start,
  input  Abort,
  input  HwReady,
  input  Capture,
  input  Transfer,
  input  Displayed,
  output [2:0] NewState
);

  wire [2:0] abortevent_1_stateout, capfinished_1_stateout, datadisplayed_1_stateout, hwrdy_1_stateout,
       selection_1_selout, startevent_1_stateout, transferdone_1_stateout;

  DataDisplayed datadisplayed_1 (
    .StateIN(OldState), .SingleShot(SingleShot), .Cont(Cont), .StateOUT(datadisplayed_1_stateout));
  TransferDone transferdone_1 (.StateIN(OldState), .StateOUT(transferdone_1_stateout));
  CapFinished capfinished_1 (.StateIN(OldState), .StateOUT(capfinished_1_stateout));
  HwRdy hwrdy_1 (.StateIN(OldState), .StateOUT(hwrdy_1_stateout));
  AbortEvent abortevent_1 (.StateOUT(abortevent_1_stateout));
  StartEvent startevent_1 (.StateIN(OldState), .StateOUT(startevent_1_stateout));
  Selection selection_1 (
    .Start(Start), .Abort(Abort), .HwReady(HwReady), .CapFinished(Capture), .TransferDone(Transfer),
    .DataDisp(Displayed), .SelOut(selection_1_selout));
  Multiplexer #(.select(3), .width(3)) multiplexer_1 (
    .in0(OldState), .in1(datadisplayed_1_stateout), .in2(transferdone_1_stateout),
    .in3(capfinished_1_stateout), .in4(hwrdy_1_stateout), .in5(abortevent_1_stateout),
    .in6(startevent_1_stateout), .out(NewState), .sel(selection_1_selout));  // open: in7
endmodule

module Selection (
  input  Start,
  input  Abort,
  input  HwReady,
  input  CapFinished,
  input  TransferDone,
  input  DataDisp,
  output [2:0] SelOut
);

  or or_1 (SelOut[0], Abort, CapFinished, DataDisp);
  or or_2 (SelOut[1], Start, CapFinished, TransferDone);
  or or_3 (SelOut[2], Start, Abort, HwReady);
endmodule

module HwRdy (
  input  [2:0] StateIN,
  output [2:0] StateOUT
);

  wire and_2_out;

  and and_1 (StateOUT[0], StateIN[0], StateIN[1]);
  and and_2 (and_2_out, StateIN[1], ~StateIN[2]);  // AND_Gate
  or or_1 (StateOUT[1], and_2_out, StateIN[0]);

  assign StateOUT[2] = StateIN[2];
endmodule

module CapFinished (
  input  [2:0] StateIN,
  output [2:0] StateOUT
);

  wire and_1_out;

  and and_1 (and_1_out, StateIN[1], ~StateIN[2]);  // AND_Gate
  or or_1 (StateOUT[0], and_1_out, StateIN[0]);
  and and_2 (StateOUT[1], StateIN[1], ~StateIN[2]);  // AND_Gate

  assign StateOUT[2] = StateIN[2];
endmodule

module TransferDone (
  input  [2:0] StateIN,
  output [2:0] StateOUT
);

  wire and_3_out;

  and and_1 (StateOUT[0], StateIN[0], ~StateIN[1]);  // AND_Gate
  and and_2 (StateOUT[1], StateIN[1], ~StateIN[0]);  // AND_Gate
  and and_3 (and_3_out, StateIN[0], StateIN[1]);
  or or_1 (StateOUT[2], and_3_out, StateIN[2]);
endmodule

module OutputLogic (
  input  [2:0] StateIn,
  output [4:0] Decoded
);

  and and_1 (Decoded[0], ~StateIn[0], ~StateIn[1], ~StateIn[2]);  // AND_Gate
  and and_2 (Decoded[1], StateIn[0], ~StateIn[1], ~StateIn[2]);  // AND_Gate
  and and_3 (Decoded[2], ~StateIn[0], StateIn[1], ~StateIn[2]);  // AND_Gate
  and and_4 (Decoded[3], StateIn[0], StateIn[1], ~StateIn[2]);  // AND_Gate
  and and_5 (Decoded[4], ~StateIn[0], ~StateIn[1], StateIn[2]);  // AND_Gate
endmodule

module DataDisplayed (
  input  [2:0] StateIN,
  input  SingleShot,
  input  Cont,
  output [2:0] StateOUT
);

  wire and_1_out;

  and and_1 (and_1_out, ~StateIN[0], ~StateIN[1], StateIN[2]);  // AND_Gate
  Multiplexer #(.width(3)) multiplexer_1 (.in0(StateIN), .in1({2'b00, Cont}), .out(StateOUT), .sel(and_1_out));

  // Notes on the sheet:
  //   Unter der Annahme, das einer der beiden Modes (Single Shot o. Cont) immer an
  //    ist (aber nur exklusiv), ist es ausreichend nur einen "Mode" zu betrachtenn
endmodule
