// Logisim project Exc1.circ as structural Verilog: 4 circuits, main circuit main
module main (
);

  wire button_1_out, button_2_out, clock_1_out;
  wire [1:0] ampel_1_fuss;
  wire [2:0] ampel_1_auto;

  Button button_1 (.out(button_1_out));
  Button button_2 (.out(button_2_out));
  Clock clock_1 (.out(clock_1_out));
  Ampel ampel_1 (
    .Button(button_1_out), .Clk(clock_1_out), .Reset(button_2_out), .Auto(ampel_1_auto), .Fuss(ampel_1_fuss));
  LED led_1 (.in(ampel_1_auto[0]));
  LED led_2 (.in(ampel_1_auto[1]));
  LED led_3 (.in(ampel_1_auto[2]));
  LED led_4 (.in(ampel_1_fuss[0]));
  LED led_5 (.in(ampel_1_fuss[1]));
endmodule

module InputLogic (
  input  Button,
  input  [2:0] OldState,
  output [2:0] NewState
);

  wire and_1_out, and_2_out, and_3_out, and_4_out;

  and and_1 (and_1_out, ~Button, ~OldState[0], ~OldState[1], ~OldState[2]);  // AND_Gate
  and and_2 (and_2_out, Button, ~OldState[0], OldState[1]);  // AND_Gate
  and and_3 (and_3_out, ~OldState[0], OldState[1]);  // AND_Gate
  and and_4 (and_4_out, OldState[0], ~OldState[1]);  // AND_Gate
  and and_5 (NewState[2], Button, ~OldState[0], ~OldState[1], ~OldState[2]);  // AND_Gate
  or or_1 (NewState[1], and_3_out, and_4_out);
  or or_2 (NewState[0], and_1_out, and_2_out);

  // Notes on the sheet:
  //   Die Logik ist einfach gehalten. Es gibt nur "Druckknopfsignal" und den State.
  //   Der Clk soll den Timer darstellen und schaltet zwischen den States.
endmodule

module Ampel (
  input  Button,
  input  Clk,
  input  Reset,
  output [2:0] Auto,
  output [1:0] Fuss
);

  wire outputlogic_1_resetbutton, s_r_ff_1_q;
  wire [2:0] inputlogic_1_newstate, register_1_q;

  S_R_Flip_Flop s_r_ff_1 (.Q(s_r_ff_1_q), .reset(outputlogic_1_resetbutton), .preset(Button));  // open: S, R, clk, Qn
  InputLogic inputlogic_1 (.Button(s_r_ff_1_q), .OldState(register_1_q), .NewState(inputlogic_1_newstate));
  Register #(.width(3)) register_1 (.D(inputlogic_1_newstate), .clk(Clk), .Q(register_1_q), .clr(Reset));  // open: en
  OutputLogic outputlogic_1 (
    .State(register_1_q), .AmpelAuto(Auto), .AmpelFuss(Fuss), .ResetButton(outputlogic_1_resetbutton));
endmodule

module OutputLogic (
  input  [2:0] State,
  output [2:0] AmpelAuto,
  output [1:0] AmpelFuss,
  output ResetButton
);

  not not_1 (AmpelAuto[0], State[1]);
  and and_1 (AmpelAuto[2], ~State[0], State[1]);  // AND_Gate
  and and_2 (AmpelFuss[1], ~State[0], ~State[1], State[2]);  // AND_Gate
  not not_2 (AmpelFuss[0], AmpelFuss[1]);

  assign AmpelAuto[1] = State[0];
  assign ResetButton = AmpelFuss[1];
endmodule
