// Logisim project Exc2.circ as structural Verilog: 4 circuits, main circuit main
module main (
);

  wire button_1_out;
  wire [1:0] statemachine_1_s0;
  wire [2:0] multiplexer_1_out;

  Button button_1 (.out(button_1_out));
  StateMachine statemachine_1 (.Taster(button_1_out), .S0(statemachine_1_s0[0]), .S1(statemachine_1_s0[1]));
  Multiplexer #(.select(2), .width(3)) multiplexer_1 (
    .in0(3'b001), .in1(3'b010), .in2(3'b011), .in3(3'b100), .out(multiplexer_1_out), .sel(statemachine_1_s0));
  // RGBLED rgbled_1: pin names not known; wires that end beside it: multiplexer_1_out[1], multiplexer_1_out[0], multiplexer_1_out[2]
endmodule

module StateMachine (
  input  Taster,
  output S0,
  output S1
);

  wire edgedetector_1_out_2;
  wire [1:0] inputlogic_1_s0_out;

  Register #(.width(2)) register_1 (
    .D(inputlogic_1_s0_out), .en(1'b1), .clk(edgedetector_1_out_2), .Q({S1, S0}));  // open: clr
  InputLogic inputlogic_1 (.S0(S0), .S1(S1), .S0_out(inputlogic_1_s0_out[0]), .S1_out(inputlogic_1_s0_out[1]));
  Edgedetector edgedetector_1 (.in_1(Taster), .out_2(edgedetector_1_out_2));
endmodule

module InputLogic (
  input  S0,
  input  S1,
  output S0_out,
  output S1_out
);

  wire and_1_out, and_2_out;

  and and_1 (and_1_out, S0, ~S1);  // AND_Gate
  and and_2 (and_2_out, ~S0, S1);  // AND_Gate
  not not_1 (S0_out, S0);
  or or_1 (S1_out, and_1_out, and_2_out);
endmodule

module Edgedetector (
  input  in_1,
  output out_2
);

  wire not_1_out, not_2_out, not_3_out;

  not not_1 (not_1_out, in_1);
  not not_2 (not_2_out, not_1_out);
  not not_3 (not_3_out, not_2_out);
  and and_1 (out_2, not_3_out, in_1);
endmodule
