// Logisim project Exc3&4.circ as structural Verilog
module PLA_BCD27Seg (
  input  [11:0] in_1
);

  wire [3:0] binary_to_bcd_converter_1_p2, binary_to_bcd_converter_1_p3, binary_to_bcd_converter_1_p4,
       binary_to_bcd_converter_1_p5;
  wire [6:0] plarom_1_p2, plarom_2_p2, plarom_3_p2, plarom_4_p2;

  // Binary_to_BCD_converter #(.binvalue(12)) binary_to_bcd_converter_1: pin names not known; wires that end beside it: in_1, binary_to_bcd_converter_1_p2, binary_to_bcd_converter_1_p3, binary_to_bcd_converter_1_p4, binary_to_bcd_converter_1_p5
  // PlaRom #(.Contents("2 0 2 0 0 2 0 0 1 0 1 0 1 1 0 0 2 2 0*4 1 0 2 1 2 0 1 2 0*3 2 1 0 1 0 2 0 0 1 2 0*4 2 2 0*4 1 0*4 2 0 1 0*6 1 0*6 1 0 0 1 1 0*3 1 0*3 1 0 0 1 0*6 1 0*8 1 0*6 1 1 0 1 0*3 1 0 0 1 0*5 1 0*6 1*3 0 0 1 0 1 1 0 0 1 0*6 1 0*6 1 0*4"), .\and (15), .outputs(7)) plarom_1: pin names not known; wires that end beside it: {binary_to_bcd_converter_1_p2[0], binary_to_bcd_converter_1_p2[1], binary_to_bcd_converter_1_p2[2], binary_to_bcd_converter_1_p2[3]}, plarom_1_p2
  // PlaRom #(.Contents("2 0 2 0 0 2 0 0 1 0 1 0 1 1 0 0 2 2 0*4 1 0 2 1 2 0 1 2 0*3 2 1 0 1 0 2 0 0 1 2 0*4 2 2 0*4 1 0*4 2 0 1 0*6 1 0*6 1 0 0 1 1 0*3 1 0*3 1 0 0 1 0*6 1 0*8 1 0*6 1 1 0 1 0*3 1 0 0 1 0*5 1 0*6 1*3 0 0 1 0 1 1 0 0 1 0*6 1 0*6 1 0*4"), .\and (15), .outputs(7)) plarom_2: pin names not known; wires that end beside it: {binary_to_bcd_converter_1_p3[0], binary_to_bcd_converter_1_p3[1], binary_to_bcd_converter_1_p3[2], binary_to_bcd_converter_1_p3[3]}, plarom_2_p2
  // PlaRom #(.Contents("2 0 2 0 0 2 0 0 1 0 1 0 1 1 0 0 2 2 0*4 1 0 2 1 2 0 1 2 0*3 2 1 0 1 0 2 0 0 1 2 0*4 2 2 0*4 1 0*4 2 0 1 0*6 1 0*6 1 0 0 1 1 0*3 1 0*3 1 0 0 1 0*6 1 0*8 1 0*6 1 1 0 1 0*3 1 0 0 1 0*5 1 0*6 1*3 0 0 1 0 1 1 0 0 1 0*6 1 0*6 1 0*4"), .\and (15), .outputs(7)) plarom_3: pin names not known; wires that end beside it: {binary_to_bcd_converter_1_p4[0], binary_to_bcd_converter_1_p4[1], binary_to_bcd_converter_1_p4[2], binary_to_bcd_converter_1_p4[3]}, plarom_3_p2
  // PlaRom #(.Contents("2 0 2 0 0 2 0 0 1 0 1 0 1 1 0 0 2 2 0*4 1 0 2 1 2 0 1 2 0*3 2 1 0 1 0 2 0 0 1 2 0*4 2 2 0*4 1 0*4 2 0 1 0*6 1 0*6 1 0 0 1 1 0*3 1 0*3 1 0 0 1 0*6 1 0*8 1 0*6 1 1 0 1 0*3 1 0 0 1 0*5 1 0*6 1*3 0 0 1 0 1 1 0 0 1 0*6 1 0*6 1 0*4"), .\and (15), .outputs(7)) plarom_4: pin names not known; wires that end beside it: {binary_to_bcd_converter_1_p5[0], binary_to_bcd_converter_1_p5[1], binary_to_bcd_converter_1_p5[2], binary_to_bcd_converter_1_p5[3]}, plarom_4_p2
  _7_Segment_Display u_7_segment_display_1 (
    .g(plarom_1_p2[0]), .f(plarom_1_p2[1]), .a(plarom_1_p2[6]), .b(plarom_1_p2[5]), .e(plarom_1_p2[2]),
    .d(plarom_1_p2[3]), .c(plarom_1_p2[4]));  // open: dp
  _7_Segment_Display u_7_segment_display_2 (
    .g(plarom_2_p2[0]), .f(plarom_2_p2[1]), .a(plarom_2_p2[6]), .b(plarom_2_p2[5]), .e(plarom_2_p2[2]),
    .d(plarom_2_p2[3]), .c(plarom_2_p2[4]));  // open: dp
  _7_Segment_Display u_7_segment_display_3 (
    .g(plarom_3_p2[0]), .f(plarom_3_p2[1]), .a(plarom_3_p2[6]), .b(plarom_3_p2[5]), .e(plarom_3_p2[2]),
    .d(plarom_3_p2[3]), .c(plarom_3_p2[4]));  // open: dp
  _7_Segment_Display u_7_segment_display_4 (
    .g(plarom_4_p2[0]), .f(plarom_4_p2[1]), .a(plarom_4_p2[6]), .b(plarom_4_p2[5]), .e(plarom_4_p2[2]),
    .d(plarom_4_p2[3]), .c(plarom_4_p2[4]));  // open: dp
endmodule

module LUT_BCD27Seg (
  input  [11:0] in_1
);

  wire binary_to_bcd_converter_1_p2, binary_to_bcd_converter_1_p3, binary_to_bcd_converter_1_p4,
       binary_to_bcd_converter_1_p5;
  wire [6:0] BCD27Seg1_out, BCD27Seg2_out, BCD27Seg3_out, BCD27Seg4_out;

  // Binary_to_BCD_converter #(.binvalue(12)) binary_to_bcd_converter_1: pin names not known; wires that end beside it: in_1, binary_to_bcd_converter_1_p2, binary_to_bcd_converter_1_p3, binary_to_bcd_converter_1_p4, binary_to_bcd_converter_1_p5
  PLA #(.in_width(4), .out_width(7), .\table ("0000 0111111\n0001 0000110\n0010 1011011\n0011 1001111\n0100 1100110\n0101 1101101\n0110 1111101\n0111 0000111\n1000 1111111\n1001 1101111\n1010 0000000\n1011 0000000\n1100 0000000\n1101 0000000\n1110 0000000\n1111 0000000")) BCD27Seg4 (
    .in(binary_to_bcd_converter_1_p2), .out(BCD27Seg4_out));
  PLA #(.in_width(4), .out_width(7), .\table ("0000 0111111\n0001 0000110\n0010 1011011\n0011 1001111\n0100 1100110\n0101 1101101\n0110 1111101\n0111 0000111\n1000 1111111\n1001 1101111\n1010 0000000\n1011 0000000\n1100 0000000\n1101 0000000\n1110 0000000\n1111 0000000")) BCD27Seg3 (
    .in(binary_to_bcd_converter_1_p3), .out(BCD27Seg3_out));
  PLA #(.in_width(4), .out_width(7), .\table ("0000 0111111\n0001 0000110\n0010 1011011\n0011 1001111\n0100 1100110\n0101 1101101\n0110 1111101\n0111 0000111\n1000 1111111\n1001 1101111\n1010 0000000\n1011 0000000\n1100 0000000\n1101 0000000\n1110 0000000\n1111 0000000")) BCD27Seg2 (
    .in(binary_to_bcd_converter_1_p4), .out(BCD27Seg2_out));
  PLA #(.in_width(4), .out_width(7), .\table ("0000 0111111\n0001 0000110\n0010 1011011\n0011 1001111\n0100 1100110\n0101 1101101\n0110 1111101\n0111 0000111\n1000 1111111\n1001 1101111\n1010 0000000\n1011 0000000\n1100 0000000\n1101 0000000\n1110 0000000\n1111 0000000")) BCD27Seg1 (
    .in(binary_to_bcd_converter_1_p5), .out(BCD27Seg1_out));
  _7_Segment_Display u_7_segment_display_1 (
    .g(BCD27Seg4_out[6]), .f(BCD27Seg4_out[5]), .a(BCD27Seg4_out[0]), .b(BCD27Seg4_out[1]),
    .e(BCD27Seg4_out[4]), .d(BCD27Seg4_out[3]), .c(BCD27Seg4_out[2]));  // open: dp
  _7_Segment_Display u_7_segment_display_2 (
    .g(BCD27Seg3_out[6]), .f(BCD27Seg3_out[5]), .a(BCD27Seg3_out[0]), .b(BCD27Seg3_out[1]),
    .e(BCD27Seg3_out[4]), .d(BCD27Seg3_out[3]), .c(BCD27Seg3_out[2]));  // open: dp
  _7_Segment_Display u_7_segment_display_3 (
    .g(BCD27Seg2_out[6]), .f(BCD27Seg2_out[5]), .a(BCD27Seg2_out[0]), .b(BCD27Seg2_out[1]),
    .e(BCD27Seg2_out[4]), .d(BCD27Seg2_out[3]), .c(BCD27Seg2_out[2]));  // open: dp
  _7_Segment_Display u_7_segment_display_4 (
    .g(BCD27Seg1_out[6]), .f(BCD27Seg1_out[5]), .a(BCD27Seg1_out[0]), .b(BCD27Seg1_out[1]),
    .e(BCD27Seg1_out[4]), .d(BCD27Seg1_out[3]), .c(BCD27Seg1_out[2]));  // open: dp
endmodule

module ROM_Logic (
  input  [1:0] in_1,
  input  [1:0] in_2
);

  wire [3:0] rom_add_1_result, rom_div_1_result, rom_mul_1_result;

  // Probe on rom_add_1_result
  ROM_ADD rom_add_1 (.A(in_1), .B(in_2), .Result(rom_add_1_result));
  // Probe on rom_mul_1_result
  ROM_MUL rom_mul_1 (.A(in_1), .B(in_2), .Result(rom_mul_1_result));
  // Probe on rom_div_1_result
  ROM_DIV rom_div_1 (.Dividend(in_1), .Divisor(in_2), .Result(rom_div_1_result));
endmodule

module ROM_ADD (
  input  [1:0] A,
  input  [1:0] B,
  output [3:0] Result
);

  ROM #(.addrWidth(4), .dataWidth(4)) Adder (.addr({B, A}), .data(Result));

  // Notes on the sheet:
  //   contents of Adder (hex, n*v repeats v):
  //   0 1 2 3 1 2 3 4 2 3 4 5 3 4 5 6
endmodule

module ROM_MUL (
  input  [1:0] A,
  input  [1:0] B,
  output [3:0] Result
);

  ROM #(.addrWidth(4), .dataWidth(4)) Mul (.addr({B, A}), .data(Result));

  // Notes on the sheet:
  //   contents of Mul (hex, n*v repeats v):
  //   5*0 1 2 3 0 2 4 6 0 3 6 9
endmodule

module ROM_DIV (
  input  [1:0] Dividend,
  input  [1:0] Divisor,
  output [3:0] Result
);

  ROM #(.addrWidth(4), .dataWidth(4)) Div (.addr({Divisor, Dividend}), .data(Result));

  // Notes on the sheet:
  //   contents of Div (hex, n*v repeats v):
  //   5*0 1 2 3 0 0 1 1 0 0 0 1
endmodule

module LED_Matrix (
  input  [3:0] BCD_In,
  output [14:0] LEDMatrixOut
);

  PLA #(.in_width(4), .out_width(15), .\table ("0000 111101101101111\n0001 001001001001001\n0010 111100111001111\n0011 111001111001111\n0100 001001111101101\n0101 111001111100111\n0110 111101111100111\n0111 001001001001111\n1000 111101111101111\n1001 111001111101111")) pla_1 (
    .in(BCD_In), .out(LEDMatrixOut));
endmodule

module LED_Matrix_Test (
  input  [3:0] in_1
);

  wire [14:0] pla_1_out;

  PLA #(.in_width(4), .out_width(15), .\table ("0000 111101101101111\n0001 001001001001001\n0010 111100111001111\n0011 111001111001111\n0100 001001111101101\n0101 111001111100111\n0110 111101111100111\n0111 001001001001111\n1000 111101111101111\n1001 111001111101111")) pla_1 (
    .in(in_1), .out(pla_1_out));
  DotMatrix #(.inputtype("row"), .matrixcols(3), .matrixrows(5)) dotmatrix_1 (
    .row0(pla_1_out[2:0]), .row1(pla_1_out[5:3]), .row2(pla_1_out[8:6]), .row3(pla_1_out[11:9]),
    .row4(pla_1_out[14:12]));
endmodule

module Clock_Led_Matrix (
);

  wire clock_1_out;
  wire [3:0] digital_clock_control_1_hour_hi, digital_clock_control_1_hour_lo,
       digital_clock_control_1_minute_hi, digital_clock_control_1_minute_lo,
       digital_clock_control_1_second_hi, digital_clock_control_1_second_lo;
  wire [14:0] led_matrix_1_ledmatrixout, led_matrix_2_ledmatrixout, led_matrix_3_ledmatrixout,
       led_matrix_4_ledmatrixout, led_matrix_5_ledmatrixout, led_matrix_6_ledmatrixout;

  Clock clock_1 (.out(clock_1_out));
  Digital_Clock_Control digital_clock_control_1 (
    .Clk(clock_1_out), .Hour_Hi(digital_clock_control_1_hour_hi), .Hour_Lo(digital_clock_control_1_hour_lo),
    .Minute_Hi(digital_clock_control_1_minute_hi), .Minute_Lo(digital_clock_control_1_minute_lo),
    .Second_Hi(digital_clock_control_1_second_hi), .Second_Lo(digital_clock_control_1_second_lo));  // open: Reset
  LED_Matrix led_matrix_1 (.BCD_In(digital_clock_control_1_hour_hi), .LEDMatrixOut(led_matrix_1_ledmatrixout));
  LED_Matrix led_matrix_2 (.BCD_In(digital_clock_control_1_hour_lo), .LEDMatrixOut(led_matrix_2_ledmatrixout));
  LED_Matrix led_matrix_3 (.BCD_In(digital_clock_control_1_minute_hi), .LEDMatrixOut(led_matrix_3_ledmatrixout));
  LED_Matrix led_matrix_4 (.BCD_In(digital_clock_control_1_minute_lo), .LEDMatrixOut(led_matrix_4_ledmatrixout));
  LED_Matrix led_matrix_5 (.BCD_In(digital_clock_control_1_second_hi), .LEDMatrixOut(led_matrix_5_ledmatrixout));
  LED_Matrix led_matrix_6 (.BCD_In(digital_clock_control_1_second_lo), .LEDMatrixOut(led_matrix_6_ledmatrixout));
  DotMatrix #(.inputtype("row"), .matrixcols(3), .matrixrows(5)) dotmatrix_1 (
    .row0(led_matrix_1_ledmatrixout[2:0]), .row1(led_matrix_1_ledmatrixout[5:3]),
    .row2(led_matrix_1_ledmatrixout[8:6]), .row3(led_matrix_1_ledmatrixout[11:9]),
    .row4(led_matrix_1_ledmatrixout[14:12]));
  DotMatrix #(.inputtype("row"), .matrixcols(3), .matrixrows(5)) dotmatrix_2 (
    .row0(led_matrix_2_ledmatrixout[2:0]), .row1(led_matrix_2_ledmatrixout[5:3]),
    .row2(led_matrix_2_ledmatrixout[8:6]), .row3(led_matrix_2_ledmatrixout[11:9]),
    .row4(led_matrix_2_ledmatrixout[14:12]));
  DotMatrix #(.inputtype("row"), .matrixcols(3), .matrixrows(5)) dotmatrix_3 (
    .row0(led_matrix_3_ledmatrixout[2:0]), .row1(led_matrix_3_ledmatrixout[5:3]),
    .row2(led_matrix_3_ledmatrixout[8:6]), .row3(led_matrix_3_ledmatrixout[11:9]),
    .row4(led_matrix_3_ledmatrixout[14:12]));
  DotMatrix #(.inputtype("row"), .matrixcols(3), .matrixrows(5)) dotmatrix_4 (
    .row0(led_matrix_4_ledmatrixout[2:0]), .row1(led_matrix_4_ledmatrixout[5:3]),
    .row2(led_matrix_4_ledmatrixout[8:6]), .row3(led_matrix_4_ledmatrixout[11:9]),
    .row4(led_matrix_4_ledmatrixout[14:12]));
  DotMatrix #(.inputtype("row"), .matrixcols(3), .matrixrows(5)) dotmatrix_5 (
    .row0(led_matrix_5_ledmatrixout[2:0]), .row1(led_matrix_5_ledmatrixout[5:3]),
    .row2(led_matrix_5_ledmatrixout[8:6]), .row3(led_matrix_5_ledmatrixout[11:9]),
    .row4(led_matrix_5_ledmatrixout[14:12]));
  DotMatrix #(.inputtype("row"), .matrixcols(3), .matrixrows(5)) dotmatrix_6 (
    .row0(led_matrix_6_ledmatrixout[2:0]), .row1(led_matrix_6_ledmatrixout[5:3]),
    .row2(led_matrix_6_ledmatrixout[8:6]), .row3(led_matrix_6_ledmatrixout[11:9]),
    .row4(led_matrix_6_ledmatrixout[14:12]));
endmodule

module Digital_Clock_Control (
  input  Reset,
  input  Clk,
  output [3:0] Hour_Hi,
  output [3:0] Hour_Lo,
  output [3:0] Minute_Hi,
  output [3:0] Minute_Lo,
  output [3:0] Second_Hi,
  output [3:0] Second_Lo
);

  wire counter_1_carry, counter_2_carry, counter_3_carry, or_1_out, or_2_out, or_3_out;
  wire [4:0] counter_3_q;
  wire [5:0] counter_1_q, counter_2_q;

  Counter #(.max('h3c), .width(6)) counter_1 (
    .clr(or_1_out), .load(1'b0), .up(1'b1), .count(1'b1), .clk(Clk), .D({6{1'b0}}), .carry(counter_1_carry),
    .Q(counter_1_q));
  or or_1 (or_1_out, counter_1_carry, Reset);
  or or_2 (or_2_out, counter_2_carry, Reset);
  Counter #(.max('h3c), .width(6)) counter_2 (
    .clr(or_2_out), .load(1'b0), .up(1'b1), .count(1'b1), .clk(counter_1_carry), .carry(counter_2_carry),
    .Q(counter_2_q));  // open: D
  or or_3 (or_3_out, counter_3_carry, Reset);
  Counter #(.max('h18), .width(5)) counter_3 (
    .clr(or_3_out), .load(1'b0), .up(1'b1), .count(1'b1), .clk(counter_2_carry), .carry(counter_3_carry),
    .Q(counter_3_q));  // open: D
  // Binary_to_BCD_converter #(.binvalue(5)) binary_to_bcd_converter_1: pin names not known; wires that end beside it: counter_3_q, Hour_Hi, Hour_Lo
  // Binary_to_BCD_converter #(.binvalue(6)) binary_to_bcd_converter_2: pin names not known; wires that end beside it: counter_2_q, Minute_Hi, Minute_Lo
  // Binary_to_BCD_converter #(.binvalue(6)) binary_to_bcd_converter_3: pin names not known; wires that end beside it: counter_1_q, Second_Hi, Second_Lo
endmodule
