// Logisim project InputCircuitVoltmeter.circ as structural Verilog: 2 circuits, main circuit InputCircuitVoltmeter
module InputCircuitVoltmeter (
  input  T1,
  input  T2,
  input  T10,
  input  T20,
  input  T100,
  input  [31:0] V_IN,
  output [11:0] ADC_OUT
);

  wire fpcomparator_1_p3;
  wire [2:0] priority_encoder_1_out;
  wire [7:0] multiplexer_1_out;
  wire [31:0] fpdivider_1_out, fpmultiplier_1_out, inttofp_1_p2, inttofp_2_p2, inttofp_3_p2,
       multiplexer_2_out;

  Priority_Encoder priority_encoder_1 (
    .in0(T1), .in1(T2), .in2(T10), .in3(T20), .in4(T100), .out(priority_encoder_1_out));  // open: in5, in6, in7, en_in, gs, en_out
  Multiplexer #(.select(3), .width(8)) multiplexer_1 (
    .in0(8'h1), .in1(8'h2), .in2(8'ha), .in3(8'h14), .in4(8'h64), .out(multiplexer_1_out),
    .sel(priority_encoder_1_out));  // open: in5, in6, in7
  // Probe on multiplexer_1_out
  // Probe on inttofp_2_p2
  // Probe on inttofp_1_p2
  // Probe on fpdivider_1_out
  // IntToFP inttofp_1: pin names not known; wires that end beside it: multiplexer_1_out, inttofp_1_p2
  FPDivider fpdivider_1 (.a(V_IN), .b(inttofp_1_p2), .out(fpdivider_1_out));
  // IntToFP #(.mode("unsigned"), .width(32)) inttofp_2: pin names not known; wires that end beside it: 32'h3e8, inttofp_2_p2
  // IntToFP #(.mode("unsigned"), .width(13)) inttofp_3: pin names not known; wires that end beside it: 13'hfff, inttofp_3_p2
  // Probe on fpmultiplier_1_out
  FPMultiplier fpmultiplier_1 (.a(fpdivider_1_out), .b(inttofp_2_p2), .out(fpmultiplier_1_out));
  Multiplexer #(.width(32)) multiplexer_2 (
    .in0(fpmultiplier_1_out), .in1(inttofp_3_p2), .out(multiplexer_2_out), .sel(fpcomparator_1_p3));
  // FPComparator fpcomparator_1: pin names not known; wires that end beside it: fpmultiplier_1_out, inttofp_3_p2, fpcomparator_1_p3
  // Probe on multiplexer_2_out
  // FPToInt #(.width(12)) fptoint_1: pin names not known; wires that end beside it: multiplexer_2_out, ADC_OUT
endmodule

module Example (
  input  [31:0] in_1,
  output [11:0] out_2
);

  wire dipswitch_1_p1, dipswitch_1_p2, dipswitch_1_p3, dipswitch_1_p4, dipswitch_1_p5;

  // DipSwitch #(.number(5)) dipswitch_1: pin names not known; wires that end beside it: dipswitch_1_p1, dipswitch_1_p2, dipswitch_1_p3, dipswitch_1_p4, dipswitch_1_p5
  InputCircuitVoltmeter inputcircuitvoltmeter_1 (
    .T1(dipswitch_1_p1), .T2(dipswitch_1_p2), .T10(dipswitch_1_p3), .T20(dipswitch_1_p4),
    .T100(dipswitch_1_p5), .V_IN(in_1), .ADC_OUT(out_2));
endmodule
