// Logisim project Solutions.circ as structural Verilog: 17 circuits, main circuit main
module main (
);

  InputCircuitVoltmeter inputcircuitvoltmeter_1 ();  // open: T1, T2, T10, T20, T100, V_IN, ADC_OUT
endmodule

module FourDigitDisplay (
  input  [9:0] in_1
);

  wire binary_to_bcd_converter_1_p4, binary_to_bcd_converter_1_p5, n7_segment_display_1_p1,
       n7_segment_display_1_p2;

  // Probe on in_1
  // _7_Segment_Display 7_segment_display_1: pin names not known; wires that end beside it: n7_segment_display_1_p1, n7_segment_display_1_p2
  // BCD_to_7_Segment_decoder bcd_to_7_segment_decoder_1: pin names not known
  // Binary_to_BCD_converter #(.binvalue(10)) binary_to_bcd_converter_1: pin names not known; wires that end beside it: in_1, n7_segment_display_1_p1, n7_segment_display_1_p2, binary_to_bcd_converter_1_p4, binary_to_bcd_converter_1_p5
  // _7_Segment_Display 7_segment_display_2: pin names not known; wires that end beside it: n7_segment_display_1_p2, binary_to_bcd_converter_1_p4
  // BCD_to_7_Segment_decoder bcd_to_7_segment_decoder_2: pin names not known
  // _7_Segment_Display 7_segment_display_3: pin names not known; wires that end beside it: binary_to_bcd_converter_1_p4, binary_to_bcd_converter_1_p5
  _7_Segment_Display u_7_segment_display_4 ();  // open: g, f, a, b, e, d, c, dp
  // BCD_to_7_Segment_decoder bcd_to_7_segment_decoder_3: pin names not known
  // BCD_to_7_Segment_decoder bcd_to_7_segment_decoder_4: pin names not known
  // Probe on n7_segment_display_1_p1
  // Probe on n7_segment_display_1_p2
  // Probe on binary_to_bcd_converter_1_p4
  // Probe on binary_to_bcd_converter_1_p5
endmodule

module FourDigitDisplay_Custom (
  input  [11:0] in_1
);

  wire bcd27seg_1_a, bcd27seg_1_b, bcd27seg_1_c, bcd27seg_1_d, bcd27seg_1_e, bcd27seg_1_f, bcd27seg_1_g,
       bcd27seg_2_a, bcd27seg_2_b, bcd27seg_2_c, bcd27seg_2_d, bcd27seg_2_e, bcd27seg_2_f, bcd27seg_2_g,
       bcd27seg_3_a, bcd27seg_3_b, bcd27seg_3_c, bcd27seg_3_d, bcd27seg_3_e, bcd27seg_3_f, bcd27seg_3_g,
       bcd27seg_4_a, bcd27seg_4_b, bcd27seg_4_c, bcd27seg_4_d, bcd27seg_4_e, bcd27seg_4_f, bcd27seg_4_g;
  wire [3:0] binary_to_bcd_converter_1_p2, binary_to_bcd_converter_1_p3, binary_to_bcd_converter_1_p4,
       binary_to_bcd_converter_1_p5;

  // Binary_to_BCD_converter #(.binvalue(12)) binary_to_bcd_converter_1: pin names not known; wires that end beside it: in_1, binary_to_bcd_converter_1_p2, binary_to_bcd_converter_1_p3, binary_to_bcd_converter_1_p4, binary_to_bcd_converter_1_p5
  // Probe on in_1
  BCD27Seg bcd27seg_1 (
    .BCD_In(binary_to_bcd_converter_1_p2), .A(bcd27seg_1_a), .B(bcd27seg_1_b), .C(bcd27seg_1_c),
    .D(bcd27seg_1_d), .E(bcd27seg_1_e), .F(bcd27seg_1_f), .G(bcd27seg_1_g));
  BCD27Seg bcd27seg_2 (
    .BCD_In(binary_to_bcd_converter_1_p3), .A(bcd27seg_2_a), .B(bcd27seg_2_b), .C(bcd27seg_2_c),
    .D(bcd27seg_2_d), .E(bcd27seg_2_e), .F(bcd27seg_2_f), .G(bcd27seg_2_g));
  BCD27Seg bcd27seg_3 (
    .BCD_In(binary_to_bcd_converter_1_p4), .A(bcd27seg_3_a), .B(bcd27seg_3_b), .C(bcd27seg_3_c),
    .D(bcd27seg_3_d), .E(bcd27seg_3_e), .F(bcd27seg_3_f), .G(bcd27seg_3_g));
  BCD27Seg bcd27seg_4 (
    .BCD_In(binary_to_bcd_converter_1_p5), .A(bcd27seg_4_a), .B(bcd27seg_4_b), .C(bcd27seg_4_c),
    .D(bcd27seg_4_d), .E(bcd27seg_4_e), .F(bcd27seg_4_f), .G(bcd27seg_4_g));
  _7_Segment_Display u_7_segment_display_1 (
    .g(bcd27seg_1_g), .f(bcd27seg_1_f), .a(bcd27seg_1_a), .b(bcd27seg_1_b), .e(bcd27seg_1_e),
    .d(bcd27seg_1_d), .c(bcd27seg_1_c));  // open: dp
  _7_Segment_Display u_7_segment_display_2 (
    .g(bcd27seg_2_g), .f(bcd27seg_2_f), .a(bcd27seg_2_a), .b(bcd27seg_2_b), .e(bcd27seg_2_e),
    .d(bcd27seg_2_d), .c(bcd27seg_2_c));  // open: dp
  _7_Segment_Display u_7_segment_display_3 (
    .g(bcd27seg_3_g), .f(bcd27seg_3_f), .a(bcd27seg_3_a), .b(bcd27seg_3_b), .e(bcd27seg_3_e),
    .d(bcd27seg_3_d), .c(bcd27seg_3_c));  // open: dp
  _7_Segment_Display u_7_segment_display_4 (
    .g(bcd27seg_4_g), .f(bcd27seg_4_f), .a(bcd27seg_4_a), .b(bcd27seg_4_b), .e(bcd27seg_4_e),
    .d(bcd27seg_4_d), .c(bcd27seg_4_c));  // open: dp
endmodule

module Voltmeter (
  input  [31:0] in_1
);

  wire dipswitch_1_p1, dipswitch_1_p2, dipswitch_1_p3, dipswitch_1_p4, dipswitch_1_p5,
       n7_segment_display_1_p2, voltmeterdigitalcircuit_1_dot1, voltmeterdigitalcircuit_1_dot2;
  wire [3:0] n7_segment_display_1_p1, n7_segment_display_1_p3, voltmeterdigitalcircuit_1_bcd1,
       voltmeterdigitalcircuit_1_bcd10;
  wire [11:0] inputcircuitvoltmeter_1_adc_out;

  // DipSwitch #(.number(5)) dipswitch_1: pin names not known; wires that end beside it: dipswitch_1_p1, dipswitch_1_p2, dipswitch_1_p3, dipswitch_1_p4, dipswitch_1_p5
  InputCircuitVoltmeter inputcircuitvoltmeter_1 (
    .T1(dipswitch_1_p1), .T2(dipswitch_1_p2), .T10(dipswitch_1_p3), .T20(dipswitch_1_p4),
    .T100(dipswitch_1_p5), .V_IN(in_1), .ADC_OUT(inputcircuitvoltmeter_1_adc_out));
  // _7_Segment_Display 7_segment_display_1: pin names not known; wires that end beside it: n7_segment_display_1_p1, n7_segment_display_1_p2, n7_segment_display_1_p3
  // BCD_to_7_Segment_decoder bcd_to_7_segment_decoder_1: pin names not known
  VoltmeterDigitalCircuit voltmeterdigitalcircuit_1 (
    .T1(dipswitch_1_p1), .T2(dipswitch_1_p2), .T10(dipswitch_1_p3), .T20(dipswitch_1_p4),
    .T100(dipswitch_1_p5), .Data(inputcircuitvoltmeter_1_adc_out), .Dot3(n7_segment_display_1_p2),
    .Dot2(voltmeterdigitalcircuit_1_dot2), .Dot1(voltmeterdigitalcircuit_1_dot1),
    .BCD1k(n7_segment_display_1_p1), .BCD100(n7_segment_display_1_p3),
    .BCD10(voltmeterdigitalcircuit_1_bcd10), .BCD1(voltmeterdigitalcircuit_1_bcd1));
  // _7_Segment_Display 7_segment_display_2: pin names not known; wires that end beside it: n7_segment_display_1_p3, voltmeterdigitalcircuit_1_dot2, voltmeterdigitalcircuit_1_bcd10
  // _7_Segment_Display 7_segment_display_3: pin names not known; wires that end beside it: voltmeterdigitalcircuit_1_bcd10, voltmeterdigitalcircuit_1_dot1, voltmeterdigitalcircuit_1_bcd1
  // BCD_to_7_Segment_decoder bcd_to_7_segment_decoder_2: pin names not known
  // BCD_to_7_Segment_decoder bcd_to_7_segment_decoder_3: pin names not known
  _7_Segment_Display u_7_segment_display_4 ();  // open: g, f, a, b, e, d, c, dp
  // BCD_to_7_Segment_decoder bcd_to_7_segment_decoder_4: pin names not known
endmodule

module InputCircuitVoltmeter (
  input  T1,
  input  T2,
  input  T10,
  input  T20,
  input  T100,
  input  [31:0] V_IN,
  output [11:0] ADC_OUT
);

  wire fpcomparator_1_p3;
  wire [2:0] priority_encoder_1_out;
  wire [7:0] multiplexer_1_out;
  wire [31:0] fpdivider_1_out, fpmultiplier_1_out, inttofp_1_p2, inttofp_2_p2, inttofp_3_p2,
       multiplexer_2_out;

  Priority_Encoder priority_encoder_1 (
    .in0(T1), .in1(T2), .in2(T10), .in3(T20), .in4(T100), .out(priority_encoder_1_out));  // open: in5, in6, in7, en_in, gs, en_out
  Multiplexer #(.select(3), .width(8)) multiplexer_1 (
    .in0(8'h1), .in1(8'h2), .in2(8'ha), .in3(8'h14), .in4(8'h64), .out(multiplexer_1_out),
    .sel(priority_encoder_1_out));  // open: in5, in6, in7
  // Probe on multiplexer_1_out
  // Probe on inttofp_2_p2
  // Probe on inttofp_1_p2
  // Probe on fpdivider_1_out
  // IntToFP inttofp_1: pin names not known; wires that end beside it: multiplexer_1_out, inttofp_1_p2
  FPDivider fpdivider_1 (.a(V_IN), .b(inttofp_1_p2), .out(fpdivider_1_out));
  // IntToFP #(.mode("unsigned"), .width(32)) inttofp_2: pin names not known; wires that end beside it: 32'h3e8, inttofp_2_p2
  // IntToFP #(.mode("unsigned"), .width(13)) inttofp_3: pin names not known; wires that end beside it: 13'hfff, inttofp_3_p2
  // Probe on fpmultiplier_1_out
  FPMultiplier fpmultiplier_1 (.a(fpdivider_1_out), .b(inttofp_2_p2), .out(fpmultiplier_1_out));
  Multiplexer #(.width(32)) multiplexer_2 (
    .in0(fpmultiplier_1_out), .in1(inttofp_3_p2), .out(multiplexer_2_out), .sel(fpcomparator_1_p3));
  // FPComparator fpcomparator_1: pin names not known; wires that end beside it: fpmultiplier_1_out, inttofp_3_p2, fpcomparator_1_p3
  // Probe on multiplexer_2_out
  // FPToInt #(.width(12)) fptoint_1: pin names not known; wires that end beside it: multiplexer_2_out, ADC_OUT
endmodule

module VoltmeterDigitalCircuit (
  input  T1,
  input  T2,
  input  T10,
  input  T20,
  input  T100,
  input  [11:0] Data,
  output Dot3,
  output Dot2,
  output Dot1,
  output [3:0] BCD1k,
  output [3:0] BCD100,
  output [3:0] BCD10,
  output [3:0] BCD1
);

  wire or_3_out;
  wire [12:0] multiplexer_1_out, multiplier_1_out;

  or or_1 (Dot3, T1, T2);
  or or_2 (Dot2, T10, T20);
  or or_3 (or_3_out, T2, T20);
  Multiplexer #(.width(13)) multiplexer_1 (.in0(13'h1), .in1(13'h2), .out(multiplexer_1_out), .sel(or_3_out));
  Multiplier #(.width(13)) multiplier_1 (
    .a(multiplexer_1_out), .b({1'b0, Data}), .out(multiplier_1_out));  // open: cin, cout
  // Binary_to_BCD_converter #(.binvalue(13)) binary_to_bcd_converter_1: pin names not known; wires that end beside it: multiplier_1_out, BCD1k, BCD100, BCD10, BCD1

  assign Dot1 = T100;
endmodule

module DigitalClock (
);

  wire button_1_out, clock_1_out;
  wire [3:0] digitalclockcontrol_1_hour_hi, digitalclockcontrol_1_hour_lo, digitalclockcontrol_1_minute_hi,
       digitalclockcontrol_1_minute_lo, digitalclockcontrol_1_second_hi, digitalclockcontrol_1_second_lo;

  Button button_1 (.out(button_1_out));
  Clock clock_1 (.out(clock_1_out));
  DigitalClockControl digitalclockcontrol_1 (
    .Reset(button_1_out), .Clk(clock_1_out), .Hour_Hi(digitalclockcontrol_1_hour_hi),
    .Hour_Lo(digitalclockcontrol_1_hour_lo), .Minute_Hi(digitalclockcontrol_1_minute_hi),
    .Minute_Lo(digitalclockcontrol_1_minute_lo), .Second_Hi(digitalclockcontrol_1_second_hi),
    .Second_Lo(digitalclockcontrol_1_second_lo));
  // _7_Segment_Display 7_segment_display_1: pin names not known; wires that end beside it: digitalclockcontrol_1_hour_hi, digitalclockcontrol_1_hour_lo
  _7_Segment_Display u_7_segment_display_2 ();  // open: g, f, a, b, e, d, c, dp
  // BCD_to_7_Segment_decoder bcd_to_7_segment_decoder_1: pin names not known
  // BCD_to_7_Segment_decoder bcd_to_7_segment_decoder_2: pin names not known
  // _7_Segment_Display 7_segment_display_3: pin names not known; wires that end beside it: digitalclockcontrol_1_minute_hi, digitalclockcontrol_1_minute_lo
  // BCD_to_7_Segment_decoder bcd_to_7_segment_decoder_3: pin names not known
  _7_Segment_Display u_7_segment_display_4 ();  // open: g, f, a, b, e, d, c, dp
  // BCD_to_7_Segment_decoder bcd_to_7_segment_decoder_4: pin names not known
  // _7_Segment_Display 7_segment_display_5: pin names not known; wires that end beside it: digitalclockcontrol_1_second_hi, digitalclockcontrol_1_second_lo
  _7_Segment_Display u_7_segment_display_6 ();  // open: g, f, a, b, e, d, c, dp
  // BCD_to_7_Segment_decoder bcd_to_7_segment_decoder_5: pin names not known
  // BCD_to_7_Segment_decoder bcd_to_7_segment_decoder_6: pin names not known
endmodule

module DigitalClockControl (
  input  Reset,
  input  Clk,
  output [3:0] Hour_Hi,
  output [3:0] Hour_Lo,
  output [3:0] Minute_Hi,
  output [3:0] Minute_Lo,
  output [3:0] Second_Hi,
  output [3:0] Second_Lo
);

  wire counter_1_carry, counter_2_carry, counter_3_carry, or_1_out, or_2_out, or_3_out;
  wire [4:0] counter_3_q;
  wire [5:0] counter_1_q, counter_2_q;

  Counter #(.max('h3c), .width(6)) counter_1 (
    .clr(or_1_out), .load(1'b0), .up(1'b1), .count(1'b1), .clk(Clk), .D({6{1'b0}}), .carry(counter_1_carry),
    .Q(counter_1_q));
  or or_1 (or_1_out, counter_1_carry, Reset);
  or or_2 (or_2_out, counter_2_carry, Reset);
  Counter #(.max('h3c), .width(6)) counter_2 (
    .clr(or_2_out), .load(1'b0), .up(1'b1), .count(1'b1), .clk(counter_1_carry), .carry(counter_2_carry),
    .Q(counter_2_q));  // open: D
  or or_3 (or_3_out, counter_3_carry, Reset);
  Counter #(.max('h18), .width(5)) counter_3 (
    .clr(or_3_out), .load(1'b0), .up(1'b1), .count(1'b1), .clk(counter_2_carry), .carry(counter_3_carry),
    .Q(counter_3_q));  // open: D
  // Binary_to_BCD_converter #(.binvalue(5)) binary_to_bcd_converter_1: pin names not known; wires that end beside it: counter_3_q, Hour_Hi, Hour_Lo
  // Binary_to_BCD_converter #(.binvalue(6)) binary_to_bcd_converter_2: pin names not known; wires that end beside it: counter_2_q, Minute_Hi, Minute_Lo
  // Binary_to_BCD_converter #(.binvalue(6)) binary_to_bcd_converter_3: pin names not known; wires that end beside it: counter_1_q, Second_Hi, Second_Lo
endmodule

module A_BAR (
  input  [3:0] BCD_In,
  output S_Out
);

  wire and_1_out, and_2_out;

  and and_1 (and_1_out, BCD_In[0], BCD_In[2]);
  and and_2 (and_2_out, ~BCD_In[0], ~BCD_In[2]);  // AND_Gate
  or or_1 (S_Out, and_1_out, and_2_out, BCD_In[1], BCD_In[3]);
endmodule

module B_BAR (
  input  [3:0] BCD_In,
  output S_Out
);

  wire and_1_out, and_2_out;

  and and_1 (and_1_out, ~BCD_In[0], ~BCD_In[1]);  // AND_Gate
  and and_2 (and_2_out, BCD_In[0], BCD_In[1]);
  or or_1 (S_Out, and_1_out, and_2_out, ~BCD_In[2]);  // OR_Gate
endmodule

module C_BAR (
  input  [3:0] BCD_In,
  output S_Out
);

  or or_1 (S_Out, BCD_In[0], ~BCD_In[1], BCD_In[2]);  // OR_Gate
endmodule

module D_BAR (
  input  [3:0] BCD_In,
  output S_Out
);

  wire and_1_out, and_2_out, and_3_out, and_4_out;

  and and_1 (and_1_out, ~BCD_In[0], BCD_In[1]);  // AND_Gate
  and and_2 (and_2_out, ~BCD_In[0], ~BCD_In[2]);  // AND_Gate
  and and_3 (and_3_out, BCD_In[1], ~BCD_In[2]);  // AND_Gate
  and and_4 (and_4_out, BCD_In[0], ~BCD_In[1], BCD_In[2]);  // AND_Gate
  or or_1 (S_Out, and_1_out, and_2_out, and_3_out, and_4_out, BCD_In[3]);
endmodule

module E_BAR (
  input  [3:0] BCD_In,
  output S_Out
);

  wire and_1_out, and_2_out;

  and and_1 (and_1_out, ~BCD_In[0], BCD_In[1]);  // AND_Gate
  and and_2 (and_2_out, ~BCD_In[0], ~BCD_In[2]);  // AND_Gate
  or or_1 (S_Out, and_1_out, and_2_out);
endmodule

module F_BAR (
  input  [3:0] BCD_In,
  output S_Out
);

  wire and_1_out, and_2_out, and_3_out;

  and and_1 (and_1_out, ~BCD_In[0], ~BCD_In[1]);  // AND_Gate
  and and_2 (and_2_out, ~BCD_In[0], BCD_In[2]);  // AND_Gate
  and and_3 (and_3_out, ~BCD_In[1], BCD_In[2]);  // AND_Gate
  or or_1 (S_Out, and_1_out, and_2_out, and_3_out, BCD_In[3]);
endmodule

module G_BAR (
  input  [3:0] BCD_In,
  output S_Out
);

  wire and_1_out, and_2_out, and_3_out;

  and and_1 (and_1_out, ~BCD_In[0], BCD_In[1]);  // AND_Gate
  and and_2 (and_2_out, BCD_In[1], ~BCD_In[2]);  // AND_Gate
  and and_3 (and_3_out, ~BCD_In[1], BCD_In[2]);  // AND_Gate
  or or_1 (S_Out, and_1_out, and_2_out, and_3_out, BCD_In[3]);
endmodule

module BCD27Seg (
  input  [3:0] BCD_In,
  output A,
  output B,
  output C,
  output D,
  output E,
  output F,
  output G
);

  A_BAR a_bar_1 (.BCD_In(BCD_In), .S_Out(A));
  B_BAR b_bar_1 (.BCD_In(BCD_In), .S_Out(B));
  C_BAR c_bar_1 (.BCD_In(BCD_In), .S_Out(C));
  D_BAR d_bar_1 (.BCD_In(BCD_In), .S_Out(D));
  E_BAR e_bar_1 (.BCD_In(BCD_In), .S_Out(E));
  F_BAR f_bar_1 (.BCD_In(BCD_In), .S_Out(F));
  G_BAR g_bar_1 (.BCD_In(BCD_In), .S_Out(G));
endmodule

module FourDigitNew (
  input  [9:0] in_1
);

  wire [3:0] binary_to_bcd_converter_1_p2, binary_to_bcd_converter_1_p3, binary_to_bcd_converter_1_p4,
       binary_to_bcd_converter_1_p5;
  wire [6:0] bcd27seg_1_a, bcd27seg_2_a, bcd27seg_3_a, bcd27seg_4_a;

  // Binary_to_BCD_converter #(.binvalue(10)) binary_to_bcd_converter_1: pin names not known; wires that end beside it: in_1, binary_to_bcd_converter_1_p2, binary_to_bcd_converter_1_p3, binary_to_bcd_converter_1_p4, binary_to_bcd_converter_1_p5
  // Probe on in_1
  BCD27Seg bcd27seg_1 (
    .BCD_In(binary_to_bcd_converter_1_p2), .A(bcd27seg_1_a[0]), .B(bcd27seg_1_a[1]), .C(bcd27seg_1_a[2]),
    .D(bcd27seg_1_a[3]), .E(bcd27seg_1_a[4]), .F(bcd27seg_1_a[5]), .G(bcd27seg_1_a[6]));
  BCD27Seg bcd27seg_2 (
    .BCD_In(binary_to_bcd_converter_1_p3), .A(bcd27seg_2_a[0]), .B(bcd27seg_2_a[1]), .C(bcd27seg_2_a[2]),
    .D(bcd27seg_2_a[3]), .E(bcd27seg_2_a[4]), .F(bcd27seg_2_a[5]), .G(bcd27seg_2_a[6]));
  BCD27Seg bcd27seg_3 (
    .BCD_In(binary_to_bcd_converter_1_p4), .A(bcd27seg_3_a[0]), .B(bcd27seg_3_a[1]), .C(bcd27seg_3_a[2]),
    .D(bcd27seg_3_a[3]), .E(bcd27seg_3_a[4]), .F(bcd27seg_3_a[5]), .G(bcd27seg_3_a[6]));
  BCD27Seg bcd27seg_4 (
    .BCD_In(binary_to_bcd_converter_1_p5), .A(bcd27seg_4_a[0]), .B(bcd27seg_4_a[1]), .C(bcd27seg_4_a[2]),
    .D(bcd27seg_4_a[3]), .E(bcd27seg_4_a[4]), .F(bcd27seg_4_a[5]), .G(bcd27seg_4_a[6]));
  _7_Segment_Display u_7_segment_display_1 (
    .g(bcd27seg_1_a[6]), .f(bcd27seg_1_a[5]), .a(bcd27seg_1_a[0]), .b(bcd27seg_1_a[1]), .e(bcd27seg_1_a[4]),
    .d(bcd27seg_1_a[3]), .c(bcd27seg_1_a[2]));  // open: dp
  _7_Segment_Display u_7_segment_display_2 (
    .g(bcd27seg_2_a[6]), .f(bcd27seg_2_a[5]), .a(bcd27seg_2_a[0]), .b(bcd27seg_2_a[1]), .e(bcd27seg_2_a[4]),
    .d(bcd27seg_2_a[3]), .c(bcd27seg_2_a[2]));  // open: dp
  _7_Segment_Display u_7_segment_display_3 (
    .g(bcd27seg_3_a[6]), .f(bcd27seg_3_a[5]), .a(bcd27seg_3_a[0]), .b(bcd27seg_3_a[1]), .e(bcd27seg_3_a[4]),
    .d(bcd27seg_3_a[3]), .c(bcd27seg_3_a[2]));  // open: dp
  _7_Segment_Display u_7_segment_display_4 (
    .g(bcd27seg_4_a[6]), .f(bcd27seg_4_a[5]), .a(bcd27seg_4_a[0]), .b(bcd27seg_4_a[1]), .e(bcd27seg_4_a[4]),
    .d(bcd27seg_4_a[3]), .c(bcd27seg_4_a[2]));  // open: dp
endmodule
